# Fritzing sketch ESP32C3_WaveGen (saved by Fritzing 0.9.3b)

parts:
  U1 = XIAO ESP32C3
  C1 = Capacitor [package=cap-pth-small2]
  R1 = Resistor [tolerance=±5% resistance=220 package="0402 [SMD]"]
  JP1 = Header 8 [package=1x08_smd]  # not connected

nets:
  N1: U1.D10, R1.Pin_0
  N2: U1.GND, C1.2
  N3: C1.1, R1.Pin_1

custom parts:
  XIAO ESP32C3: Seeed Studio XIAO ESP32C3 adopts new RISC-V architecture, supporting both Wi-Fi and BLE wireless connectivities. For Internet of Things applications, you will find it is flexible and suitable for all kinds of IoT scenarios.
